# Fritzing sketch project (saved by Fritzing 0.9.2b)

parts:
  BAT1 = BC9VPC [package=bc9vpc]
  Part1 = Arduino Uno (Rev3)
  Water_Level_Sensor1 = Water Level Sensor
  SG1 = Buzzer 12mm [package=buzzer-12mm-ns]

nets:
  N1: BAT1.V+, Part1.VIN
  GND: BAT1.V-, Part1.GND, Water_Level_Sensor1.GND, SG1.2
  N2: Part1.A5/SCL, Water_Level_Sensor1.SIG
  N3: Part1.D4, Water_Level_Sensor1.VCC
  N4: Part1.D5_PWM, SG1.1

custom parts:
  Water Level Sensor: A water level sensor. This sensor operates at 3V to 5V. The Sig (signal) pin outputs an analogue signal that is in proportion to the amount of water in contact with the sensor.
