# Fritzing sketch project (saved by Fritzing 0.9.2b)
breadboards: 2

parts:
  U1 = ESP8266 NodeMCU LoLin module
  Sensor1 = Gas Sensor Breakout Board
  Part1 = Adafruit SCD4x [part_number="Adafruit #5187"]

nets:
  N1: U1.D1, Part1.SCL
  N2: U1.D2, Part1.SDA
  3V3: U1.3V3, Sensor1.5V, Part1.3.3V
  GND: U1.GND, Sensor1.GND, Part1.GND
  N3: U1.A0, Sensor1.AOUT

custom parts:
  ESP8266 NodeMCU LoLin module: ESP8266 based NodeMCU
  Gas Sensor Breakout Board: Gas sensor breakout board. Input voltage is 5V. Sensor output is available in analog and digital.
  Adafruit SCD4x: Take a deep breath in...now slowly breathe out. Mmm isn't it wonderful? All that air around us, which we bring into our lungs, extracts oxygen from and then breathes out carbon dioxide. CO2 is essential for life on this planet we call Earth - we and plants take turns using and emitting CO2 in an elegant symbiosis. But it's important to keep that CO2 balanced - you don't want too much around,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
